# Fritzing sketch AS3935_ESP32 (saved by Fritzing 0.9.4)

parts:
  SparkFun_AS3935_Lightning_Detector1 = SparkFun AS3935 Lightning Detector
  Part1 = node32s

nets:
  GND: SparkFun_AS3935_Lightning_Detector1.GND, Part1.GND
  3.3V: SparkFun_AS3935_Lightning_Detector1.3.3V, Part1.3.3V
  N1: SparkFun_AS3935_Lightning_Detector1.INT, Part1.IO4
  N2: SparkFun_AS3935_Lightning_Detector1.SCLK/SCL, Part1.IO22
  N3: SparkFun_AS3935_Lightning_Detector1.MOSI/SDA, Part1.IO21

notes:
  SI

custom parts:
  SparkFun AS3935 Lightning Detector: The SparkFun Lightning Detector adds lightning detection to your next weather station to make sure you are aware of any potential hazardous weather heading your way. The AS3935 is capable of detecting lightning up to 40km away with an accuracy of 1km to the storm front with a sensitive antenna tuned to pick up lightning events in the 500kHz band. There are a number of sources that can cause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
