# Fritzing sketch one-wire-ESP32 (saved by Fritzing 0.9.4)

parts:
  DS1 = DS18B20 1-Wire Temperature Sensor [part_number=DS18B20]
  Part1 = node32s
  DS2 = DS18B20 1-Wire Temperature Sensor [part_number=DS18B20]  # not connected
  R1 = Resistor [tolerance=±5% resistance=220 package="0805 [SMD]"]  # not connected
  DS3 = DS18B20 1-Wire Temperature Sensor [part_number=DS18B20]  # not connected
  DS4 = DS18B20 1-Wire Temperature Sensor [part_number=DS18B20]  # not connected
  DS6 = DS18B20 1-Wire Temperature Sensor [part_number=DS18B20]  # not connected

nets:
  VDD: DS1.VDD, Part1.5V
  N1: DS1.DQ, Part1.IO15
  GND: DS1.GND, Part1.GND

notes:
  4.7K ohm
  Data wire
