# Fritzing sketch ML8511-ESP32 (saved by Fritzing 0.9.4)

parts:
  Part1 = node32s
  Part2 = ML8511 Breakout Board

nets:
  3.3V: Part1.3.3V, Part2.3V3
  N1: Part1.IO34, Part2.EN
  N2: Part1.IO32, Part2.OUT
  GND: Part1.GND, Part2.GND

notes:
  ML8511
  EN
  Out

custom parts:
  ML8511 Breakout Board: This breakout board uses the ML8511 UV (ultraviolet) light sensor. The ML8511 works best with light in the 280-390nm wavelengths. The board operates at 2.7 to 3.6V.
