# Fritzing sketch SDS011-ESp32 (saved by Fritzing 0.9.4)

parts:
  SDS1 = SDS011 - dust sensor [part_number=1]
  Part1 = node32s

nets:
  N1: SDS1.TX, Part1.RXD
  GND: SDS1.GND, Part1.GND
  5V: SDS1.5v, Part1.5V

custom parts:
  SDS011 - dust sensor: The SDS 011 Sensor is a quite recent Air Quality Sensor developed by inovafit, a spin-off from the university of Jinan (in Shandong). With its size, it is probably one of the best sensor in terms of accuracy: While other sensors tend to focus on shrinking the sensor size, the SDS 011 has opted for a size tradeoff allowing it to use a larger fan. And the larger the fan, the better the quality.
