# Fritzing sketch Waveshare4_2-ESP32 (saved by Fritzing 0.9.4)

parts:
  U4 = Display [part_number=0532610819 package=Picoblade-53261-0819]  # not connected
  U5 = Display [part_number=0532610819 package=Picoblade-53261-0819]
  U6 = Display [part_number=0532610819 package=Picoblade-53261-0819]  # not connected
  Part1 = node32s

nets:
  N1: U5.BUSY, Part1.IO4
  N2: U5.RST, Part1.IO16
  N3: U5.DC, Part1.IO17
  N4: U5.CS, Part1.IO5
  N5: U5.CLK, Part1.IO18
  N6: U5.DIN, Part1.IO23
  GND: U5.GND, Part1.GND
  3V3: U5.3V3, Part1.3.3V

notes:
  Waveshare 4.2inch e-Paper
  Display
  7.5 inch e-Paper
  Display

custom parts:
  Display: Molex Picoblade Header: 1.25mm Pitch Miniature Crimping Connector. Single Row Straight Pin Header (SMT)
