# Fritzing sketch ultrasonic-HC-SR04-ESP32 (saved by Fritzing 0.9.4)

parts:
  hc-sr1 = hc-sr04
  Part1 = node32s

nets:
  VCC: hc-sr1.VCC, Part1.5V
  N1: hc-sr1.Trig, Part1.IO26
  N2: hc-sr1.Echo, Part1.IO27
  GND: hc-sr1.GND, Part1.GND
